// Logisim project 16bit_CPU.circ as structural Verilog
module project_alu (
  input  [15:0] A,
  input  [15:0] B,
  input  ALU_OE,
  input  [3:0] AUSel,
  input  [2:0] RUSel,
  output [15:0] AUResult,
  output [15:0] AUDout,
  output RUResult
);

  project_ao project_ao_1 (.A(A), .B(B), .ALU_OE(ALU_OE), .AUSel(AUSel), .AUResult(AUResult), .AUDout(AUDout));
  project_ro project_ro_1 (.A(A), .B(B), .RUSel(RUSel), .RUResult(RUResult));
endmodule

module project_ao (
  input  [15:0] A,
  input  [15:0] B,
  input  ALU_OE,
  input  [3:0] AUSel,
  output [15:0] AUResult,
  output [15:0] AUDout
);

  wire [15:0] adder_1_out, and_1_out, divider_1_out, divider_2_rem, multiplexer_1_out, multiplier_1_out,
       negator_1_out, negator_2_out, or_1_out, shifter_1_out, shifter_2_out, shifter_3_out, shifter_4_out,
       subtractor_1_out, xor_1_out;

  Adder #(.width(16)) adder_1 (.a(A), .b(B), .out(adder_1_out));  // open: cin, cout
  assign and_1_out = A & B;  // AND_Gate and_1, 16 bits wide
  assign or_1_out = A | B;  // OR_Gate or_1, 16 bits wide
  assign xor_1_out = A ^ B;  // XOR_Gate xor_1, 16 bits wide
  Divider #(.width(16)) divider_1 (.a(A), .b(B), .out(divider_1_out));  // open: upper, rem
  Divider #(.width(16)) divider_2 (.a(A), .b(B), .rem(divider_2_rem));  // open: out, upper
  Multiplier #(.width(16)) multiplier_1 (.a(A), .b(B), .out(multiplier_1_out));  // open: cin, cout
  Subtractor #(.width(16)) subtractor_1 (.a(A), .b(B), .out(subtractor_1_out));  // open: bin, bout
  Shifter #(.width(16)) shifter_1 (.in(A), .\dist (4'b0010), .out(shifter_1_out));
  Shifter #(.width(16)) shifter_2 (.in(B), .\dist (4'b0010), .out(shifter_2_out));
  Shifter #(.shift("lr"), .width(16)) shifter_3 (.in(A), .\dist (4'b0010), .out(shifter_3_out));
  Shifter #(.shift("lr"), .width(16)) shifter_4 (.in(B), .\dist (4'b0010), .out(shifter_4_out));
  Negator #(.width(16)) negator_1 (.in(A), .out(negator_1_out));
  Negator #(.width(16)) negator_2 (.in(B), .out(negator_2_out));
  Multiplexer #(.select(4), .width(16)) multiplexer_1 (
    .in0(adder_1_out), .in1(and_1_out), .in2(or_1_out), .in3(xor_1_out), .in4(divider_1_out),
    .in5(divider_2_rem), .in6(multiplier_1_out), .in7(subtractor_1_out), .in8(shifter_1_out),
    .in9(shifter_2_out), .in10(shifter_3_out), .in11(shifter_4_out), .in12(negator_1_out),
    .in13(negator_2_out), .out(multiplexer_1_out), .sel(AUSel));  // open: in14, in15
  assign AUDout = ALU_OE ? multiplexer_1_out : 16'bz;  // Controlled_Buffer controlled_buffer_1

  assign AUResult = AUDout;
endmodule

module project_ro (
  input  [15:0] A,
  input  [15:0] B,
  input  [2:0] RUSel,
  output RUResult
);

  wire comparator_1_eq, comparator_1_gt, comparator_1_lt, not_1_out, or_1_out, or_2_out;

  Comparator #(.width(16)) comparator_1 (
    .a(A), .b(B), .gt(comparator_1_gt), .eq(comparator_1_eq), .lt(comparator_1_lt));
  or or_1 (or_1_out, comparator_1_gt, comparator_1_eq);
  or or_2 (or_2_out, comparator_1_eq, comparator_1_lt);
  not not_1 (not_1_out, comparator_1_eq);
  Multiplexer #(.select(3)) multiplexer_1 (
    .in0(comparator_1_gt), .in1(comparator_1_eq), .in2(or_1_out), .in3(comparator_1_lt), .in4(or_2_out),
    .in5(not_1_out), .out(RUResult), .sel(RUSel));  // open: in6, in7
endmodule

module Datapath (
  input  WE_MAR,
  input  Reset_MAR,
  input  OE_MAR,
  input  [15:0] TestData,
  input  Test_OE,
  input  internal_OE_MBR,
  input  WE_IR,
  input  clk,
  input  Reset_IR,
  input  WE_MBR,
  input  OE_IR,
  input  Reset_MBR,
  input  OE_MBR,
  input  WE_A,
  input  Reg_AB_Reset,
  input  Reg_AB_OE,
  input  WE_OR,
  input  Reset_OR,
  input  ALU_OE,
  input  [3:0] AUSel,
  input  OE_OR,
  input  [2:0] RUSel,
  input  WE_B,
  output [7:0] Result_MAR,
  output [15:0] IR_Result,
  output [15:0] Result_MBR,
  output [15:0] Result_A,
  output [15:0] Result_OR,
  output [15:0] AUResult,
  output RUResult,
  output [15:0] Result_B
);

  wire [7:0] bitselector_1_out, Instruction_Register_eight_lsbs, mar_1_dout;
  wire [15:0] ALU_audout;

  register_file Instruction_Register (
    .Data(ALU_audout), .WE(WE_IR), .clk(clk), .reset(Reset_IR), .OE(OE_IR), .Result(IR_Result),
    .Eight_LSBs(Instruction_Register_eight_lsbs));  // open: Dout, Eight_MSBs
  register_file A (
    .Data(ALU_audout), .WE(WE_A), .clk(clk), .reset(Reg_AB_Reset), .OE(Reg_AB_OE), .Result(Result_A));  // open: Dout, Eight_LSBs, Eight_MSBs
  project_alu ALU (
    .A(Result_A), .B(Result_B), .ALU_OE(ALU_OE), .AUSel(AUSel), .RUSel(RUSel), .AUResult(AUResult),
    .AUDout(ALU_audout), .RUResult(RUResult));
  register_file B (
    .Data(ALU_audout), .WE(WE_B), .clk(clk), .reset(Reg_AB_Reset), .OE(Reg_AB_OE), .Result(Result_B));  // open: Dout, Eight_LSBs, Eight_MSBs
  BitSelector #(.group(8)) bitselector_1 (.in(Instruction_Register_eight_lsbs), .out(bitselector_1_out), .sel(1'b0));
  LED led_1 (.in(ALU_audout[15]));
  LED led_2 (.in(ALU_audout[14]));
  assign ALU_audout = Test_OE ? TestData : 16'bz;  // Controlled_Buffer controlled_buffer_1
  LED led_3 (.in(ALU_audout[13]));
  LED led_4 (.in(ALU_audout[12]));
  LED led_5 (.in(ALU_audout[11]));
  LED led_6 (.in(ALU_audout[10]));
  LED led_7 (.in(ALU_audout[9]));
  LED led_8 (.in(ALU_audout[8]));
  LED led_9 (.in(ALU_audout[7]));
  LED led_10 (.in(ALU_audout[6]));
  LED led_11 (.in(ALU_audout[5]));
  LED led_12 (.in(ALU_audout[4]));
  LED led_13 (.in(ALU_audout[3]));
  LED led_14 (.in(ALU_audout[2]));
  LED led_15 (.in(ALU_audout[1]));
  LED led_16 (.in(ALU_audout[0]));
  assign ALU_audout = internal_OE_MBR ? Result_MBR : 16'bz;  // Controlled_Buffer controlled_buffer_2
  MAR mar_1 (
    .Data(bitselector_1_out), .WE(WE_MAR), .clk(clk), .reset(Reset_MAR), .OE(OE_MAR), .Result(Result_MAR),
    .Dout(mar_1_dout));
  register_file MBR (
    .Data(ALU_audout), .WE(WE_MBR), .clk(clk), .reset(Reset_MBR), .OE(OE_MBR), .Result(Result_MBR));  // open: Dout, Eight_LSBs, Eight_MSBs
  register_file Output_Register (
    .Data(ALU_audout), .WE(WE_OR), .clk(clk), .reset(Reset_OR), .OE(OE_OR), .Result(Result_OR),
    .Dout(ALU_audout));  // open: Eight_LSBs, Eight_MSBs

  // Notes on the sheet:
  //   D14
  //   D15
  //   D13
  //   D12
  //   D11
  //   D10
  //   D9
  //   D8
  //   D7
  //   D6
  //   D5
  //   D4
  //   D3
  //   D2
  //   D1
  //   D0
endmodule

module register_file (
  input  [15:0] Data,
  input  WE,
  input  clk,
  input  reset,
  input  OE,
  output [15:0] Result,
  output [15:0] Dout,
  output [7:0] Eight_LSBs,
  output [7:0] Eight_MSBs
);

  Register #(.width(16)) register_1 (.D(Data), .en(WE), .clk(clk), .Q(Result), .clr(reset));
  assign Dout = OE ? Result : 16'bz;  // Controlled_Buffer controlled_buffer_1
  BitSelector #(.group(8), .width(16)) bitselector_1 (.in(Dout), .out(Eight_LSBs), .sel(1'b0));
  BitSelector #(.group(8), .width(16)) bitselector_2 (.in(Dout), .out(Eight_MSBs), .sel(1'b1));
endmodule

module CPU (
);

  Datapath datapath_1 ();  // open: WE_MAR, Reset_MAR, OE_MAR, TestData, Test_OE, internal_OE_MBR, WE_IR, clk, Reset_IR, WE_MBR, OE_IR, Reset_MBR, OE_MBR, WE_A, Reg_AB_Reset, Reg_AB_OE, WE_OR, Reset_OR, ALU_OE, AUSel, OE_OR, RUSel, WE_B, Result_MAR, IR_Result, Result_MBR, Result_A, Result_OR, AUResult, RUResult, Result_B
endmodule

module MAR (
  input  [7:0] Data,
  input  WE,
  input  clk,
  input  reset,
  input  OE,
  output [7:0] Result,
  output [7:0] Dout
);

  Register register_1 (.D(Data), .en(WE), .clk(clk), .Q(Result), .clr(reset));
  assign Dout = OE ? Result : 8'bz;  // Controlled_Buffer controlled_buffer_1
endmodule
